# Fritzing sketch gate controller schematic (saved by Fritzing 0.9.3b)
breadboards: 1

parts:
  Open_button = Round Pushbutton
  Close_button = Round Pushbutton
  Open_LED = smd LED [color="Green (555nm)" package="1206 [SMD]"]
  External_Limit_Switch = Square Pushbutton
  12V_to_5V = RioRand LM2596
  R1 = Resistor [tolerance=±5% resistance=220 package=THT]
  R2 = Resistor [tolerance=±5% resistance=220 package=THT]
  WeMos_D1_Mini1 = WeMos D1 Mini
  12V_In = Power Jack [package=power_jack_pth_lock]
  Close_LED = LED - 5mm [color="Red (633nm)" package="5 mm [THT]"]
  Relay = KY-019 5V Relay Module [package="Breakout board"]
  Relay_2 = KY-019 5V Relay Module [package="Breakout board"]
  to_Linear_Actuator = Power Jack [package=power_jack_pth_lock]

nets:
  N1: Open_button.leg0, WeMos_D1_Mini1.D6
  N2: Open_button.leg1, Close_button.leg1, Open_LED.cathode, External_Limit_Switch.leg1, 12V_to_5V.Pin_4, WeMos_D1_Mini1.G, Close_LED.cathode, Relay.-, Relay_2.-
  N3: Close_button.leg0, WeMos_D1_Mini1.D7
  N4: Open_LED.anode, R1.Pin_0
  N5: External_Limit_Switch.leg0, WeMos_D1_Mini1.D2
  N6: 12V_to_5V.Pin_1, 12V_In.PWR, Relay.NO, Relay_2.NC
  GND: 12V_to_5V.Pin_2, 12V_In.GND, Relay.NC, Relay_2.NO, to_Linear_Actuator.GND
  N7: 12V_to_5V.Pin_3, WeMos_D1_Mini1.5V
  N8: R1.Pin_1, WeMos_D1_Mini1.D5
  N9: R2.Pin_0, Close_LED.anode
  N10: R2.Pin_1, WeMos_D1_Mini1.D8
  N11: WeMos_D1_Mini1.3V3, Relay.+, Relay_2.+
  N12: WeMos_D1_Mini1.D3, Relay_2.S
  N13: WeMos_D1_Mini1.D4, Relay.S
  N14: Relay.Common, Relay_2.Common, to_Linear_Actuator.PWR

custom parts:
  WeMos D1 Mini: The D1 mini is a mini wifi board based on ESP-8266EX.
  KY-019 5V Relay Module: KY-019 5V Relay module, used to control AC circuits.
